# Fritzing sketch weather_station (saved by Fritzing 0.9.2b)
circuit board: 8.46667cm x 5.64444cm
breadboards: 2

parts:
  Part1 = Arduino Uno (Rev3)
  LCD1 = LCD screen
  RHT1 = Humidity and Temperature Sensor RHT03
  R1 = Resistor [tolerance=±5% resistance=470 package="0805 [SMD]"]
  R2 = Resistor [tolerance=±5% resistance=4.7k package="0805 [SMD]"]
  R3 = Resistor [tolerance=±5% resistance=220 package="0805 [SMD]"]
  R4 = Resistor [tolerance=±5% resistance=10k package="0805 [SMD]"]
  Part2 = RFM12B
  Part3 = JeeNode wireless microcontroller
  BMP1 = BMP085 Breakout
  RHT2 = Humidity and Temperature Sensor RHT03
  S1 = Pushbutton [package="[THT]"]
  R5 = Resistor [tolerance=±5% resistance=1k package="0603 [SMD]"]

nets (from the breadboard view):
  N1: Part1.A2, LCD1.LED+
  N2: Part1.A3, S1.Pin_3, S1.Pin_4, R5.Pin_1
  N3: Part1.A4/SDA, BMP1.SDA
  N4: Part1.A5/SCL, BMP1.SCL
  N5: Part1.D8, LCD1.E
  N6: Part1.D9_PWM, LCD1.DB4
  N7: Part1.D10_PWM/SS, Part2.SEL
  N8: Part1.D11_PWM/MOSI, Part2.SDI
  N9: Part1.D12/MISO, Part2.SDO
  N10: Part1.D13/SCK, Part2.SCK
  N11: Part1.D2, Part2.IRQ
  N12: Part1.D3_PWM, R4.Pin_1, RHT2.Data-signal
  N13: Part1.D4, LCD1.DB5
  N14: Part1.D5_PWM, LCD1.DB6
  N15: Part1.D6_PWM, LCD1.DB7
  N16: Part1.D7, LCD1.RS
  5V: Part1.5V, LCD1.VDD, R3.Pin_0, Part2.5V, BMP1.VIN, S1.Pin_1, S1.Pin_2
  GND: Part1.GND, LCD1.VSS, LCD1.R/W, LCD1.LED-, R1.Pin_1, Part2.GND, BMP1.GND, R5.Pin_0
  N17: LCD1.V0, R1.Pin_0, R2.Pin_0
  N18: RHT1.Vcc, Part3.PWR
  N19: RHT1.Data-signal, Part3.DIO1
  N20: RHT1.GND_2, Part3.GND
  N21: R2.Pin_1, R3.Pin_1
  N22: R4.Pin_0, RHT2.Vcc

custom parts:
  BMP085 Breakout: A breakout for the BMP085 barometric pressure and temperature sensor
